// Logisim project 2BooleanExpression.circ as structural Verilog: 1 circuit, main circuit main
module main (
  input  W,
  input  X,
  input  Y,
  input  Z,
  output F
);

  wire and_1_out, and_2_out, and_3_out, and_4_out, and_5_out, not_1_out, not_2_out, not_3_out;

  not not_1 (not_1_out, W);
  not not_2 (not_2_out, X);
  not not_3 (not_3_out, Y);
  and and_1 (and_1_out, X, not_3_out, Z);
  and and_2 (and_2_out, not_2_out, not_3_out, Z);
  and and_3 (and_3_out, not_1_out, X, Y);
  and and_4 (and_4_out, W, not_2_out, Y);
  and and_5 (and_5_out, W, X, Y);
  or or_1 (F, and_1_out, and_2_out, and_3_out, and_4_out, and_5_out);
endmodule
