// Logisim project 2Simplified.circ as structural Verilog: 1 circuit, main circuit main
module main (
  input  W,
  input  X,
  input  Y,
  input  Z,
  output F
);

  wire and_1_out, and_2_out, and_3_out, not_1_out;

  not not_1 (not_1_out, Y);
  and and_1 (and_1_out, not_1_out, Z);
  and and_2 (and_2_out, X, Y);
  and and_3 (and_3_out, W, Y);
  or or_1 (F, and_1_out, and_2_out, and_3_out);
endmodule
