// Logisim project CounterFrom0to7.circ as structural Verilog: 1 circuit, main circuit main
// TA0
module main (
);

  wire and_1_out, clock_1_out, TA0_q, TA1_q;

  Clock clock_1 (.out(clock_1_out));
  and and_1 (and_1_out, TA1_q, TA0_q);
  T_Flip_Flop TA2 (.clk(clock_1_out), .T(and_1_out));  // open: Q, Qn, preset, reset, en
  T_Flip_Flop TA1 (.clk(clock_1_out), .T(TA0_q), .Q(TA1_q));  // open: Qn, preset, reset, en
  T_Flip_Flop TA0 (.clk(clock_1_out), .T(1'b1), .Q(TA0_q));  // open: Qn, preset, reset, en
endmodule
