// Logisim project CounterFrom7to0.circ as structural Verilog: 1 circuit, main circuit main
module main (
);

  wire and_1_out, clock_1_out, TA0_q, TA0_qn, TA1_qn;

  Clock clock_1 (.out(clock_1_out));
  T_Flip_Flop TA2 (.clk(clock_1_out), .T(and_1_out));  // open: Q, Qn, preset, reset, en
  T_Flip_Flop TA1 (.clk(clock_1_out), .T(TA0_qn), .Qn(TA1_qn));  // open: Q, preset, reset, en
  and and_1 (and_1_out, TA1_qn, TA0_qn);
  T_Flip_Flop TA0 (.clk(clock_1_out), .T(1'b1), .Q(TA0_q), .Qn(TA0_qn));  // open: preset, reset, en
endmodule
