// Logisim project 1NAND.circ as structural Verilog: 1 circuit, main circuit main
module main (
  input  D,
  input  C,
  input  B,
  input  A,
  output F
);

  wire nand_1_out, nand_2_out, nand_3_out, nand_4_out, nand_5_out, nand_6_out, nand_7_out;

  nand nand_1 (nand_1_out, D, D);
  nand nand_2 (nand_2_out, C, C);
  nand nand_3 (nand_3_out, B, B);
  nand nand_4 (nand_4_out, A, A);
  nand nand_5 (nand_5_out, nand_4_out, nand_3_out, nand_1_out);
  nand nand_6 (nand_6_out, B, nand_2_out, nand_1_out);
  nand nand_7 (nand_7_out, A, nand_3_out, nand_2_out, D);
  nand nand_8 (F, nand_5_out, nand_6_out, nand_7_out);
endmodule
