// Logisim project 1NOR.circ as structural Verilog: 1 circuit, main circuit main
module main (
  input  D,
  input  C,
  input  B,
  input  A,
  output F
);

  wire nor_1_out, nor_2_out, nor_3_out, nor_4_out, nor_5_out, nor_6_out, nor_7_out, nor_8_out, nor_9_out;

  nor nor_1 (nor_1_out, D, D);
  nor nor_2 (nor_2_out, C, C);
  nor nor_3 (nor_3_out, B, B);
  nor nor_4 (nor_4_out, A, A);
  nor nor_5 (nor_5_out, nor_3_out, nor_2_out);
  nor nor_6 (nor_6_out, nor_4_out, nor_2_out);
  nor nor_7 (nor_7_out, A, nor_1_out);
  nor nor_8 (nor_8_out, nor_3_out, nor_1_out);
  nor nor_9 (nor_9_out, nor_4_out, B, D);
  nor nor_10 (F, nor_5_out, nor_6_out, nor_7_out, nor_8_out, nor_9_out);
endmodule
