// Logisim project 1SOP.circ as structural Verilog: 1 circuit, main circuit main
module main (
  input  A,
  input  B,
  input  C,
  input  D,
  output F
);

  wire and_1_out, and_2_out, and_3_out, and_4_out, and_5_out, not_1_out, not_2_out, not_3_out;

  not not_1 (not_1_out, A);
  not not_2 (not_2_out, B);
  not not_3 (not_3_out, D);
  and and_1 (and_1_out, B, C);
  and and_2 (and_2_out, A, C);
  and and_3 (and_3_out, not_1_out, D);
  and and_4 (and_4_out, B, D);
  and and_5 (and_5_out, A, not_2_out, not_3_out);
  or or_1 (F, and_1_out, and_2_out, and_3_out, and_4_out, and_5_out);
endmodule
